# Fritzing sketch Pedalino (saved by Fritzing 0.9.3b)
circuit board: 10cm x 6cm
breadboards: 2

parts:
  LCD_16x2 = LCD screen
  Pedalino(TM)_Shield = Arduino Mega 2560 (Rev3)
  Componente2 = Bluetooth HC-05 Macho
  IR_Receiver = IR Receiver Breakout [package=PCB]
  R2 = Resistor [tolerance=±5% resistance=1 package=THT]
  S1 = Pushbutton [package="[THT]"]
  R6 = Rotary Potentiometer (Small) [maximum_resistance=100kΩ package=THT]
  S2 = Pushbutton [package="[THT]"]
  S3 = Pushbutton [package="[THT]"]
  S4 = Pushbutton [package="[THT]"]
  R3 = Rotary Potentiometer (Small) [maximum_resistance=10kΩ package=THT]
  LED1 = LED - 5mm [color="Blue (430nm)" package="5 mm [THT]"]
  R1 = Resistor [tolerance=±5% resistance=220 package=THT]
  R7 = Resistor [tolerance=±5% resistance=220 package=THT]
  R4 = Resistor [tolerance=±5% resistance=220 package=THT]
  DIN1 = DIN-5 jack (MIDI) [package=THT]
  R8 = Resistor [tolerance=±5% resistance=220 package=THT]

nets:
  GND: LCD_16x2.VSS, LCD_16x2.R/W, Pedalino(TM)_Shield.GND, Componente2.GND, IR_Receiver.GND, R2.Pin_0, S1.Pin_1, S1.Pin_2, R6.leg1, S2.Pin_1, S2.Pin_2, S3.Pin_1, S3.Pin_2, S4.Pin_1, S4.Pin_2, R3.leg1, LED1.cathode, R1.Pin_0, DIN1.2
  VCC: LCD_16x2.VDD, Pedalino(TM)_Shield.5V, Componente2.VCC, IR_Receiver.VCC, R6.leg2, R3.leg2, R4.Pin_0
  N1: LCD_16x2.V0, R2.Pin_1
  N2: LCD_16x2.RS, Pedalino(TM)_Shield.D53
  N3: LCD_16x2.E, Pedalino(TM)_Shield.D51
  N4: LCD_16x2.DB4, Pedalino(TM)_Shield.D49
  N5: LCD_16x2.DB5, Pedalino(TM)_Shield.D47
  N6: LCD_16x2.DB6, Pedalino(TM)_Shield.D45
  N7: LCD_16x2.DB7, Pedalino(TM)_Shield.D43
  N8: LCD_16x2.LED+, Pedalino(TM)_Shield.D41
  N9: LCD_16x2.LED-, R1.Pin_1
  N10: Pedalino(TM)_Shield.A0, R3.wiper
  N11: Pedalino(TM)_Shield.A1, R6.wiper
  N12: Pedalino(TM)_Shield.A2, S1.Pin_3, S1.Pin_4
  N13: Pedalino(TM)_Shield.A3, S2.Pin_3, S2.Pin_4
  N14: Pedalino(TM)_Shield.A4, S3.Pin_3, S3.Pin_4
  N15: Pedalino(TM)_Shield.A5, S4.Pin_3, S4.Pin_4
  N16: Pedalino(TM)_Shield.D17_PWM/RX2, Componente2.TXD
  N17: Pedalino(TM)_Shield.D16_PWM/TX2, Componente2.RXD
  N18: Pedalino(TM)_Shield.D14/TX3, R8.Pin_1
  N19: Pedalino(TM)_Shield.D33, IR_Receiver.OUT
  N20: Pedalino(TM)_Shield.D35, R7.Pin_0
  N21: LED1.anode, R7.Pin_1
  N22: R4.Pin_1, DIN1.4
  N23: DIN1.5, R8.Pin_0
