# Fritzing sketch PedalinoESP32-LCDKeypadShield (saved by Fritzing 0.9.3b)
circuit board: 10.1776cm x 5.36194cm
breadboards: 2

parts:
  Pedalino(TM)_Shield = Arduino Mega 2560 (Rev3)
  R4 = Resistor [tolerance=±5% resistance=220 package=THT]
  MIDI_OUT = DIN-5 jack (MIDI) [package=THT]
  IR_Receiver = KY-022 Infrared Receiver Module [package="Breakout board"]
  R8 = Resistor [tolerance=±5% resistance=220 package=THT]
  IC1 = 6n137 Optocoupler [package="DIP (Dual Inline) [THT]"]
  MIDI_IN = DIN-5 jack (MIDI) [package=THT]
  R9 = Resistor [tolerance=±5% resistance=220 package=THT]
  D1 = Rectifier Diode [part_number=1N4007 package="300 mil [THT]"]
  R10 = Resistor [tolerance=±5% resistance=10k package=THT]
  part = ESP32S-HiLetgo [part_number=ESP32S-HiLetgo]
  Componente1 = Bluetooth HM-10
  Componente2 = LCD Keypad Shield  # not connected

nets:
  N1: Pedalino(TM)_Shield.D19/RX1, Componente1.TXD
  N2: Pedalino(TM)_Shield.D18/TX1, Componente1.RXD
  N3: Pedalino(TM)_Shield.D17_PWM/RX2, IC1.Vo, R10.Pin_1
  N4: Pedalino(TM)_Shield.D16_PWM/TX2, R8.Pin_1
  N5: Pedalino(TM)_Shield.D15/RX3, part.GPIO17
  N6: Pedalino(TM)_Shield.D14/TX3, part.GPIO16
  VIN: Pedalino(TM)_Shield.5V, R4.Pin_0, IR_Receiver.Vin, IC1.Vcc, R10.Pin_0, part.VIN, Componente1.VCC
  N7: Pedalino(TM)_Shield.D24, IR_Receiver.S
  GND: Pedalino(TM)_Shield.GND, MIDI_OUT.2, IR_Receiver.-, IC1.GND, part.GND, Componente1.GND
  N8: R4.Pin_1, MIDI_OUT.4
  N9: MIDI_OUT.5, R8.Pin_0
  N10: IC1.NC#0, IC1.Vf+, R9.Pin_1
  N11: IC1.Vf-, MIDI_IN.5, D1.anode
  N12: MIDI_IN.4, R9.Pin_0

custom parts:
  KY-022 Infrared Receiver Module: Arduino IR receiver module KY-022, reacts to 38kHz infrared light.
  6n137 Optocoupler: 6n137 fast Optocoupler. With 8 pins on a 300mil dual inline package (DIP) footprint. Ve is strobe input. Output is inverting.
  ESP32S-HiLetgo: HiLetgo ESP-WROOM-32 ESP32 ESP-32S Development Board 2.4GHz Dual-Mode WiFi + Bluetooth Dual Cores Microcontroller The ESP32 integrated with Antenna switches, RF Balun, power amplifiers, low-noise amplifiers, filters, and management modules, and the entire solution occupies the least area of PCB. 2.4 GHz Wi-Fi plus Bluetooth dual-mode chip, with TSMC Ultra-low power consumption 40nm technology,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
  LCD Keypad Shield: It consists of a 1602 white character blue backlight LCD. The keypad consists of 5 keys — select, up, right, down and left. To save the digital IO pins, the keypad interface uses only one ADC channel. The key value is read through a 5 stage voltage divider.
