# Fritzing sketch PedalinoESP32 (saved by Fritzing 0.9.3b)
circuit board: 10.1776cm x 5.36194cm
breadboards: 3

parts:
  LCD_16x2 = LCD screen
  Pedalino(TM)_Shield = Arduino Mega 2560 (Rev3)
  R2 = Resistor [tolerance=±5% resistance=1k package=THT]
  R4 = Resistor [tolerance=±5% resistance=220 package=THT]
  MIDI_OUT = DIN-5 jack (MIDI) [package=THT]
  IR_Receiver = KY-022 Infrared Receiver Module [package="Breakout board"]
  R8 = Resistor [tolerance=±5% resistance=220 package=THT]
  IC1 = 6n137 Optocoupler [package="DIP (Dual Inline) [THT]"]
  MIDI_IN = DIN-5 jack (MIDI) [package=THT]
  R9 = Resistor [tolerance=±5% resistance=220 package=THT]
  D1 = Rectifier Diode [part_number=1N4007 package="300 mil [THT]"]
  R1 = Resistor [tolerance=±5% resistance=220 package=THT]
  R10 = Resistor [tolerance=±5% resistance=10k package=THT]
  part = ESP32S-HiLetgo [part_number=ESP32S-HiLetgo]
  Componente1 = Bluetooth HM-10

nets:
  GND: LCD_16x2.VSS, LCD_16x2.R/W, Pedalino(TM)_Shield.GND, R2.Pin_0, MIDI_OUT.2, IR_Receiver.-, IC1.GND, R1.Pin_0, part.GND, Componente1.GND
  VIN: LCD_16x2.VDD, Pedalino(TM)_Shield.5V, R4.Pin_0, IR_Receiver.Vin, IC1.Vcc, R10.Pin_0, part.VIN, Componente1.VCC
  N1: LCD_16x2.V0, R2.Pin_1
  N2: LCD_16x2.RS, Pedalino(TM)_Shield.D50
  N3: LCD_16x2.E, Pedalino(TM)_Shield.D48
  N4: LCD_16x2.DB4, Pedalino(TM)_Shield.D42
  N5: LCD_16x2.DB5, Pedalino(TM)_Shield.D40
  N6: LCD_16x2.DB6, Pedalino(TM)_Shield.D38
  N7: LCD_16x2.DB7, Pedalino(TM)_Shield.D36
  N8: LCD_16x2.LED+, Pedalino(TM)_Shield.D44
  N9: LCD_16x2.LED-, R1.Pin_1
  N10: Pedalino(TM)_Shield.D19/RX1, Componente1.TXD
  N11: Pedalino(TM)_Shield.D18/TX1, Componente1.RXD
  N12: Pedalino(TM)_Shield.D17_PWM/RX2, IC1.Vo, R10.Pin_1
  N13: Pedalino(TM)_Shield.D16_PWM/TX2, R8.Pin_1
  N14: Pedalino(TM)_Shield.D15/RX3, part.GPIO17
  N15: Pedalino(TM)_Shield.D14/TX3, part.GPIO16
  N16: Pedalino(TM)_Shield.D2_PWM, IR_Receiver.S
  N17: R4.Pin_1, MIDI_OUT.4
  N18: MIDI_OUT.5, R8.Pin_0
  N19: IC1.NC#0, IC1.Vf+, R9.Pin_1
  N20: IC1.Vf-, MIDI_IN.5, D1.anode
  N21: MIDI_IN.4, R9.Pin_0

custom parts:
  KY-022 Infrared Receiver Module: Arduino IR receiver module KY-022, reacts to 38kHz infrared light.
  6n137 Optocoupler: 6n137 fast Optocoupler. With 8 pins on a 300mil dual inline package (DIP) footprint. Ve is strobe input. Output is inverting.
  ESP32S-HiLetgo: HiLetgo ESP-WROOM-32 ESP32 ESP-32S Development Board 2.4GHz Dual-Mode WiFi + Bluetooth Dual Cores Microcontroller The ESP32 integrated with Antenna switches, RF Balun, power amplifiers, low-noise amplifiers, filters, and management modules, and the entire solution occupies the least area of PCB. 2.4 GHz Wi-Fi plus Bluetooth dual-mode chip, with TSMC Ultra-low power consumption 40nm technology,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
