# Fritzing sketch PedalinoESP8266-LCDKeypadShield (saved by Fritzing 0.9.3b)
circuit board: 10.1776cm x 5.36194cm
breadboards: 2

parts:
  Pedalino(TM)_Shield = Arduino Mega 2560 (Rev3)
  R4 = Resistor [tolerance=±5% resistance=220 package=THT]
  MIDI_OUT = DIN-5 jack (MIDI) [package=THT]
  IR_Receiver = KY-022 Infrared Receiver Module [package="Breakout board"]
  R8 = Resistor [tolerance=±5% resistance=220 package=THT]
  IC1 = 6n137 Optocoupler [package="DIP (Dual Inline) [THT]"]
  MIDI_IN = DIN-5 jack (MIDI) [package=THT]
  R9 = Resistor [tolerance=±5% resistance=220 package=THT]
  D1 = Rectifier Diode [part_number=1N4007 package="300 mil [THT]"]
  R10 = Resistor [tolerance=±5% resistance=10k package=THT]
  Bluetooth_UART = Bluetooth HM-10 [part_number=" Communication Module"]
  Componente2 = LCD Keypad Shield  # not connected
  ESP-01_1M = ESP8266 WiFi Module [part_number=ESP8266]
  3_3V_Power = DC-DC Power Module (3.3v) [part_number="Supply Module"]
  Flash = Momentary Switch [package=ksa_sealed_tac_switch]
  Reset = Momentary Switch [package=ksa_sealed_tac_switch]
  R12 = Resistor [tolerance=±5% resistance=10k package=THT]
  R13 = Resistor [tolerance=±5% resistance=10k package=THT]
  R14 = Resistor [tolerance=±5% resistance=10k package=THT]

nets:
  N1: Pedalino(TM)_Shield.D19/RX1, Bluetooth_UART.TXD
  N2: Pedalino(TM)_Shield.D18/TX1, Bluetooth_UART.RXD
  N3: Pedalino(TM)_Shield.D17_PWM/RX2, IC1.Vo, R10.Pin_1
  N4: Pedalino(TM)_Shield.D16_PWM/TX2, R8.Pin_1
  N5: Pedalino(TM)_Shield.D15/RX3, ESP-01_1M.TXD
  N6: Pedalino(TM)_Shield.D14/TX3, ESP-01_1M.RXD
  VIN: Pedalino(TM)_Shield.5V, R4.Pin_0, IR_Receiver.Vin, IC1.Vcc, R10.Pin_0, Bluetooth_UART.VCC, 3_3V_Power.Vin
  N7: Pedalino(TM)_Shield.D24, IR_Receiver.S
  GND: Pedalino(TM)_Shield.GND, MIDI_OUT.2, IR_Receiver.-, IC1.GND, Bluetooth_UART.GND, 3_3V_Power.GND
  N8: R4.Pin_1, MIDI_OUT.4
  N9: MIDI_OUT.5, R8.Pin_0
  N10: IC1.NC#0, IC1.Vf+, R9.Pin_1
  N11: IC1.Vf-, MIDI_IN.5, D1.anode
  N12: MIDI_IN.4, R9.Pin_0
  N13: ESP-01_1M.VCC, 3_3V_Power.Vout, R12.Pin_0, R13.Pin_0, R14.Pin_0
  N14: ESP-01_1M.GPIO_0, Flash.1, R13.Pin_1
  N15: ESP-01_1M.RST, Reset.1, R12.Pin_1
  N16: ESP-01_1M.CH_PD, R14.Pin_1
  N17: ESP-01_1M.GND, 3_3V_Power.GND*, Flash.3, Reset.3

custom parts:
  KY-022 Infrared Receiver Module: Arduino IR receiver module KY-022, reacts to 38kHz infrared light.
  6n137 Optocoupler: 6n137 fast Optocoupler. With 8 pins on a 300mil dual inline package (DIP) footprint. Ve is strobe input. Output is inverting.
  LCD Keypad Shield: It consists of a 1602 white character blue backlight LCD. The keypad consists of 5 keys — select, up, right, down and left. To save the digital IO pins, the keypad interface uses only one ADC channel. The key value is read through a 5 stage voltage divider.
  ESP8266 WiFi Module: Generic WiFi Module based on the ESP8266 with onboard PCB antenna and UART communications
  DC-DC Power Module (3.3v): DC-DC Power Module based con AMS1117-3.3 Input: DC 4.5~7V (input power must higher 1V than output power); Output: 3.3V (+/-0.05V error), 800mA
