# Fritzing sketch PedalinoESP8266-Uno (saved by Fritzing 0.9.3b)
circuit board: 10.1776cm x 5.36194cm
breadboards: 2

parts:
  R4 = Resistor [tolerance=±5% resistance=220 package=THT]
  MIDI_OUT = DIN-5 jack (MIDI) [package=THT]
  R8 = Resistor [tolerance=±5% resistance=220 package=THT]
  IC1 = 6n137 Optocoupler [package="DIP (Dual Inline) [THT]"]
  MIDI_IN = DIN-5 jack (MIDI) [package=THT]
  R9 = Resistor [tolerance=±5% resistance=220 package=THT]
  D1 = Rectifier Diode [part_number=1N4007 package="300 mil [THT]"]
  R10 = Resistor [tolerance=±5% resistance=10k package=THT]
  ESP-01_1M = ESP8266 WiFi Module [part_number=ESP8266]
  3_3V_Power = DC-DC Power Module (3.3v) [part_number="Supply Module"]
  Flash = Momentary Switch [package=ksa_sealed_tac_switch]
  Reset = Momentary Switch [package=ksa_sealed_tac_switch]
  R12 = Resistor [tolerance=±5% resistance=10k package=THT]
  R13 = Resistor [tolerance=±5% resistance=10k package=THT]
  R14 = Resistor [tolerance=±5% resistance=10k package=THT]
  Componente1 = Arduino Uno (Rev3)

nets:
  VCC: R4.Pin_0, IC1.Vcc, R10.Pin_0, 3_3V_Power.Vin, Componente1.5V
  N1: R4.Pin_1, MIDI_OUT.4
  N2: MIDI_OUT.5, R8.Pin_0
  GND: MIDI_OUT.2, IC1.GND, 3_3V_Power.GND, Componente1.GND
  N3: R8.Pin_1, Componente1.D9_PWM
  N4: IC1.NC#0, IC1.Vf+, R9.Pin_1
  N5: IC1.Vf-, MIDI_IN.5, D1.anode
  N6: IC1.Vo, R10.Pin_1, Componente1.D10_PWM/SS
  N7: MIDI_IN.4, R9.Pin_0
  N8: ESP-01_1M.RXD, Componente1.D11_PWM/MOSI
  N9: ESP-01_1M.VCC, 3_3V_Power.Vout, R12.Pin_0, R13.Pin_0, R14.Pin_0
  N10: ESP-01_1M.GPIO_0, Flash.1, R13.Pin_1
  N11: ESP-01_1M.RST, Reset.1, R12.Pin_1
  N12: ESP-01_1M.CH_PD, R14.Pin_1
  N13: ESP-01_1M.GND, 3_3V_Power.GND*, Flash.3, Reset.3
  N14: ESP-01_1M.TXD, Componente1.D12/MISO

custom parts:
  6n137 Optocoupler: 6n137 fast Optocoupler. With 8 pins on a 300mil dual inline package (DIP) footprint. Ve is strobe input. Output is inverting.
  ESP8266 WiFi Module: Generic WiFi Module based on the ESP8266 with onboard PCB antenna and UART communications
  DC-DC Power Module (3.3v): DC-DC Power Module based con AMS1117-3.3 Input: DC 4.5~7V (input power must higher 1V than output power); Output: 3.3V (+/-0.05V error), 800mA
