# Fritzing sketch PedalinoESP8266 (saved by Fritzing 0.9.3b)
circuit board: 10.1776cm x 5.36194cm
breadboards: 2

parts:
  LCD_16x2 = LCD screen
  Pedalino(TM)_Shield = Arduino Mega 2560 (Rev3)
  R2 = Resistor [tolerance=±5% resistance=1k package=THT]
  R4 = Resistor [tolerance=±5% resistance=220 package=THT]
  MIDI_OUT = DIN-5 jack (MIDI) [package=THT]
  IR_Receiver = KY-022 Infrared Receiver Module [package="Breakout board"]
  R8 = Resistor [tolerance=±5% resistance=220 package=THT]
  ESP-01_1M = ESP8266 WiFi Module [part_number=ESP8266]
  IC1 = 6n137 Optocoupler [package="DIP (Dual Inline) [THT]"]
  MIDI_IN = DIN-5 jack (MIDI) [package=THT]
  R9 = Resistor [tolerance=±5% resistance=220 package=THT]
  D1 = Rectifier Diode [part_number=1N4007 package="300 mil [THT]"]
  R1 = Resistor [tolerance=±5% resistance=220 package=THT]
  3_3V_Power_Supply_Module = DC-DC Power Module (3.3v)
  R10 = Resistor [tolerance=±5% resistance=10k package=THT]
  Componente1 = Bluetooth HM-10

nets:
  GND: LCD_16x2.VSS, LCD_16x2.R/W, Pedalino(TM)_Shield.GND, R2.Pin_0, MIDI_OUT.2, IR_Receiver.-, ESP-01_1M.GND, IC1.GND, R1.Pin_0, 3_3V_Power_Supply_Module.GND, 3_3V_Power_Supply_Module.GND*, Componente1.GND
  VIN: LCD_16x2.VDD, Pedalino(TM)_Shield.5V, R4.Pin_0, IR_Receiver.Vin, IC1.Vcc, 3_3V_Power_Supply_Module.Vin, R10.Pin_0, Componente1.VCC
  N1: LCD_16x2.V0, R2.Pin_1
  N2: LCD_16x2.RS, Pedalino(TM)_Shield.D50
  N3: LCD_16x2.E, Pedalino(TM)_Shield.D48
  N4: LCD_16x2.DB4, Pedalino(TM)_Shield.D42
  N5: LCD_16x2.DB5, Pedalino(TM)_Shield.D40
  N6: LCD_16x2.DB6, Pedalino(TM)_Shield.D38
  N7: LCD_16x2.DB7, Pedalino(TM)_Shield.D36
  N8: LCD_16x2.LED+, Pedalino(TM)_Shield.D44
  N9: LCD_16x2.LED-, R1.Pin_1
  N10: Pedalino(TM)_Shield.D19/RX1, Componente1.TXD
  N11: Pedalino(TM)_Shield.D18/TX1, Componente1.RXD
  N12: Pedalino(TM)_Shield.D17_PWM/RX2, IC1.Vo, R10.Pin_1
  N13: Pedalino(TM)_Shield.D16_PWM/TX2, R8.Pin_1
  N14: Pedalino(TM)_Shield.D15/RX3, ESP-01_1M.TXD
  N15: Pedalino(TM)_Shield.D14/TX3, ESP-01_1M.RXD
  N16: Pedalino(TM)_Shield.D2_PWM, IR_Receiver.S
  N17: R4.Pin_1, MIDI_OUT.4
  N18: MIDI_OUT.5, R8.Pin_0
  N19: ESP-01_1M.VCC, ESP-01_1M.CH_PD
  N20: IC1.Vf+, R9.Pin_1, D1.cathode
  N21: IC1.Vf-, MIDI_IN.5, D1.anode
  N22: MIDI_IN.4, R9.Pin_0

custom parts:
  KY-022 Infrared Receiver Module: Arduino IR receiver module KY-022, reacts to 38kHz infrared light.
  ESP8266 WiFi Module: Generic WiFi Module based on the ESP8266 with onboard PCB antenna and UART communications
  6n137 Optocoupler: 6n137 fast Optocoupler. With 8 pins on a 300mil dual inline package (DIP) footprint. Ve is strobe input. Output is inverting.
  DC-DC Power Module (3.3v): DC-DC Power Module based con AMS1117-3.3 Input: DC 4.5~7V (input power must higher 1V than output power); Output: 3.3V (+/-0.05V error), 800mA
